# Fritzing sketch Proyek_Mini (saved by Fritzing 0.9.3b)
breadboards: 1

parts:
  Part1 = Arduino Uno (Rev3) - ICSP
  Display1 = LCD screen 16x2 IIC [part_number=101290]
  LED1 = smd LED [color="Red (633nm)" package="1206 [SMD]"]
  R1 = Resistor [tolerance=±5% resistance=220 package="0603 [SMD]"]
  VALVE1 = Plastic Solenoid Valve
  U1 = Voltage Regulator - 5V [package="TO220 [THT]"]
  D2 = Diode [package=diode-hv]
  JACK1 = 2.1mm Barrel Jack with Terminal Block
  R2 = Resistor [tolerance=±5% resistance=220 package="0603 [SMD]"]

nets:
  N1: Part1.A4/SDA, Display1.SDA
  N2: Part1.A5/SCL, Display1.SCL
  GND: Part1.GND, Display1.GND, LED1.cathode
  N3: Part1.D3_PWM, R2.Pin_1
  N4: Part1.D4, R1.Pin_0
  5V: Part1.5V, Display1.VCC
  N5: LED1.anode, R1.Pin_1
  N6: VALVE1.no_name_yet#1, U1.GND, D2.C
  N7: VALVE1.no_name_yet#2, JACK1.NEG
  N8: U1.input_voltage, R2.Pin_0
  N9: U1.output_voltage, JACK1.POS

custom parts:
  LCD screen 16x2 IIC: LCD screen with HD44780 controller enables showing text, symbols, value or anything else that comes from Croduino/Arduino. It is capable of showing 16 symbols in two lines and therefore can be used in many projects that need to send clearly visible and legible output information.. • Color of symbols: White • Backlight: Blue • Dimensions: 80 x 36 x 12 mm • Screen dimensions: 64.5 x 16 mm •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
